# Fritzing sketch Seguidor_PanTilt_stepper2015 (saved by Fritzing 0.9.1b)
circuit board: 8.46667cm x 5.64444cm
stripboards: 1

parts:
  Parte1 = Arduino Uno (Rev3)
  Q1 = TRANSISTOR_NPN [package=to-92]
  Q2 = TRANSISTOR_NPN [package=to-92]
  M2 = Stepper Motor - Bipolar
  Power_plug1 = Power plug
  R1 = Resistor [tolerance=±5% resistance=1k package=THT]
  R2 = Resistor [tolerance=±5% resistance=10k package=THT]
  R3 = Resistor [tolerance=±5% resistance=1k package=THT]
  R4 = Resistor [tolerance=±5% resistance=10k package=THT]
  Parte2 = L298 Module

nets (from the breadboard view):
  GND: Parte1.GND, Q1.E, Q2.E, Power_plug1.GND, Parte2.GND
  N1: Parte1.D0/RX, R1.Pin_1, Parte2.IN1
  N2: Parte1.D1/TX, R3.Pin_1, Parte2.IN3
  VIN: Parte1.VIN, Power_plug1.VCC, Parte2.12V
  N3: Q1.B, R1.Pin_0
  N4: Q1.C, R2.Pin_1, Parte2.IN2
  N5: Q2.B, R3.Pin_0
  N6: Q2.C, R4.Pin_0, Parte2.IN4
  N7: M2.A, Parte2.OUT1
  N8: M2.C, Parte2.OUT2
  N9: M2.B, Parte2.OUT3
  N10: M2.D, Parte2.OUT4
  N11: R2.Pin_0, R4.Pin_1, Parte2.5V

notes:
  Duplicar:
  Un L298N para cada motor
  Alimentación 5V-3A
  PIN0- Stepper Motor1
  PIN1-Stepper Motor 1
  PIN2- Enable Motor 1
  PIN3- Stepper Motor2
  PIN4-Stepper Motor 2
  PIN5- Enable Motor 2
  PIN6- Final Carrera Motor 1-Norte
  PIN7-Final Carrera Motor1-Sur
  PIN8- Final Carrera Motor 2-Este
  AIN3-Final Carrera Motor 2-Oeste
  PIN 9-13 con NRF24L01
  AIN4 - AIN 5 con Tyny RTC I2C
  El segundo motor va a la entradas del arudino 3,4 y 5
  Conectados a ENA y ENB
  Fuente DC 5V-2A

custom parts:
  L298 Module: Módulo Ponte H com L298(Corrente Máxima 2A)
