# Fritzing sketch Seguidor_PanTilt_stepper2015_FinalesCarrera (saved by Fritzing 0.9.1b)
stripboards: 1

parts:
  Parte1 = Arduino Uno (Rev3)
  S1 = SWITCH-MOMENTARY-2 [package=tactile-switch-1101ne]
  R7 = Resistor [tolerance=±5% resistance=10k package=THT]
  S2 = SWITCH-MOMENTARY-2 [package=tactile_switch_smd]
  R8 = Resistor [tolerance=±5% resistance=10k package=THT]  # not connected
  S3 = SWITCH-MOMENTARY-2 [package=tactile_switch_smd]
  S4 = SWITCH-MOMENTARY-2 [package=tactile_switch_smd]
  R9 = Resistor [tolerance=±5% resistance=10k package=THT]
  R10 = Resistor [tolerance=±5% resistance=10k package=THT]  # not connected

nets (from the schematic view):
  N1: Parte1.A3, S4.1
  N2: Parte1.D8, S3.1, R9.Pin_0
  N3: Parte1.D6_PWM, S1.1
  N4: Parte1.D7, R7.Pin_0, S2.1
  N5: Parte1.5V, S1.2, S2.2, S3.2, S4.2
  N6: Parte1.GND, R9.Pin_1

notes:
  Duplicar:
  Un L298N para cada motor
  Alimentación 5V-3A
  PIN0- Stepper Motor1
  PIN1-Stepper Motor 1
  PIN2- Enable Motor 1
  PIN3- Stepper Motor2
  PIN4-Stepper Motor 2
  PIN5- Enable Motor 2
  PIN6- Final Carrera Motor 1-Norte
  PIN7-Final Carrera Motor1-Sur
  PIN8- Final Carrera Motor 2-Este
  AIN3-Final Carrera Motor 2-Oeste
  PIN 9-13 con NRF24L01
  AIN4 - AIN 5 con Tyny RTC I2C
