# Fritzing sketch Seguidor_PanTilt_stepper2015_NRF24 (saved by Fritzing 0.9.1b)
stripboards: 1

parts:
  Parte1 = Arduino Uno (Rev3)
  NRF24L1 = NRF24L01

nets:
  N1: Parte1.D9_PWM, NRF24L1.CE
  N2: Parte1.D10_PWM/SS, NRF24L1.CSN
  N3: Parte1.D11_PWM/MOSI, NRF24L1.MOSI
  N4: Parte1.D12/MISO, NRF24L1.MISO
  N5: Parte1.D13/SCK, NRF24L1.SCK
  3V3: Parte1.3V3, NRF24L1.VCC
  GND: Parte1.GND, NRF24L1.GND

notes:
  1 - GND
  2 - VCC 3.3V !!! NOT 5V
  3 - CE to Arduino pin 9
  4 - CSN to Arduino pin 10
  5 - SCK to Arduino pin 13
  6 - MOSI to Arduino pin 11
  7 - MISO to Arduino pin 12
  8 - UNUSED

custom parts:
  NRF24L01: NRF24L01 module
