# Fritzing sketch Seguidor_PanTilt_stepper2015_TynyRTC_I2C (saved by Fritzing 0.9.1b)
stripboards: 1

parts:
  Parte1 = Arduino Uno (Rev3)
  Tiny_RTC1 = Tiny RTC

nets:
  N1: Parte1.A4/SDA, Tiny_RTC1.SDA
  N2: Parte1.A5/SCL, Tiny_RTC1.SCL
  5V: Parte1.5V, Tiny_RTC1.VCC
  GND: Parte1.GND, Tiny_RTC1.GND

notes:
  Reloj RTC Tyny RTC I2C
  - SCL a A4
  - DS a A5

custom parts:
  Tiny RTC: Tiny RTC I2C module DS1370Z RTC and AT24C32 EEPROM
